// Logisim project adder.circ as structural Verilog: 2 circuits, main circuit Half_Adder
module Half_Adder (
  input  A,
  input  B,
  input  C_In,
  output S,
  output C_Out
);

  wire and_1_out, and_2_out, xor_1_out;

  xor xor_1 (xor_1_out, A, B);
  xor xor_2 (S, xor_1_out, C_In);
  and and_1 (and_1_out, C_In, xor_1_out);
  and and_2 (and_2_out, A, B);
  or or_1 (C_Out, and_1_out, and_2_out);
endmodule

module Full_Adder_8_bit (
  input  A0,
  input  B0,
  input  C_In,
  input  A1,
  input  B1,
  input  A2,
  input  B2,
  input  A3,
  input  B3,
  input  A4,
  input  B4,
  input  A5,
  input  B5,
  input  A6,
  input  B6,
  input  A7,
  input  B7,
  output S0,
  output S1,
  output S2,
  output S3,
  output S4,
  output S5,
  output S6,
  output S7,
  output C_Out
);

  wire half_adder_1_c_out, half_adder_2_c_out, half_adder_3_c_out, half_adder_4_c_out, half_adder_5_c_out,
       half_adder_6_c_out, half_adder_7_c_out;

  Half_Adder half_adder_1 (.A(A0), .B(B0), .C_In(C_In), .S(S0), .C_Out(half_adder_1_c_out));
  Half_Adder half_adder_2 (.A(A1), .B(B1), .C_In(half_adder_1_c_out), .S(S1), .C_Out(half_adder_2_c_out));
  Half_Adder half_adder_3 (.A(A2), .B(B2), .C_In(half_adder_2_c_out), .S(S2), .C_Out(half_adder_3_c_out));
  Half_Adder half_adder_4 (.A(A3), .B(B3), .C_In(half_adder_3_c_out), .S(S3), .C_Out(half_adder_4_c_out));
  Half_Adder half_adder_5 (.A(A4), .B(B4), .C_In(half_adder_4_c_out), .S(S4), .C_Out(half_adder_5_c_out));
  Half_Adder half_adder_6 (.A(A5), .B(B5), .C_In(half_adder_5_c_out), .S(S5), .C_Out(half_adder_6_c_out));
  Half_Adder half_adder_7 (.A(A6), .B(B6), .C_In(half_adder_6_c_out), .S(S6), .C_Out(half_adder_7_c_out));
  Half_Adder half_adder_8 (.A(A7), .B(B7), .C_In(half_adder_7_c_out), .S(S7), .C_Out(C_Out));
endmodule
